# Fritzing sketch AttinyServoProgramming (saved by Fritzing 0.9.0b)
perfboards: 1

parts:
  C1 = Electrolytic Capacitor [capacitance=10µF package="100 mil [THT, electrolytic]"]
  J1 = female pin header, 8 pins [form="♀ (female)"]
  J2 = female pin header, 5 pins [form="♀ (female)"]  # not connected
  J3 = female pin header, 5 pins [form="♀ (female)"]  # not connected
  U1 = attiny85 [package=dip]  # not connected
  J4 = screw terminal, 4 pins  # not connected
  Arduino1 = Arduino Uno (Rev3)

nets:
  N1: C1.+, Arduino1.RESET
  N2: J1.pin1, Arduino1.GND

notes:
  Arduino --> AttinyServo
  GND --> GND
  Power --> Vcc
  10 --> Reset
  13 --> 2 --> SCK
  12 --> 1 --> MISO
  11 --> 0 --> MOSI
  Arduino 10uf Reset -> GND
